# Fritzing sketch projeto_07_arduino_web (saved by Fritzing 0.9.0b)

parts:
  J1 = Basic Servo
  Componente2 = Arduino Leonardo (Rev3b)
  LED2 = smd LED [color="Red (633nm)" package="0603 [SMD]"]

nets:
  GND: J1.gnd, Componente2.GND, LED2.cathode
  VCC: J1.vcc, Componente2.5V
  N1: J1.pulse, Componente2.D9_PWM/A9
  N2: Componente2.D13_PWM, LED2.anode
